// Logisim project VRAC.circ as structural Verilog: 9 circuits, main circuit main
module main (
  input  clock,
  input  reset
);

  wire alu_1_eq, alu_1_le, alu_1_overflow, check_jump_1_jump, control_unit_1_altregpos,
       control_unit_1_alusrc, control_unit_1_incrstackaddr, control_unit_1_memsrc, control_unit_1_regwrite,
       control_unit_1_regwritesrc, control_unit_1_usestack, flags_1_eq_out, flags_1_le_out, or_1_out,
       or_2_out, or_3_out, or_4_out, or_5_out, or_6_out;
  wire [1:0] control_unit_1_regwritemod;
  wire [2:0] control_unit_1_inst_size;
  wire [3:0] control_unit_1_memread, control_unit_1_memwrite, multiplexer_2_out, multiplexer_3_out;
  wire [4:0] control_unit_1_jump, undriven_4;
  wire [5:0] undriven_3;
  wire [7:0] multiplexer_5_out, multiplexer_11_out, multiplexer_12_out, multiplexer_13_out,
       multiplexer_14_out, register_file_1_r1d_2, undriven, undriven_2;
  wire [7:3] undriven_5;
  wire [15:0] adder_1_out, bit_extender_1_out, multiplexer_1_out, register_1_q;
  wire [23:0] multiplexer_5_out_2, register_file_1_r1d;
  wire [31:0] adder_2_out, alu_1_data, bit_extender_2_out, multiplexer_4_out, multiplexer_6_out,
       multiplexer_7_out, multiplexer_8_out, multiplexer_9_out, multiplexer_10_out, multiplexer_15_out,
       or_7_out, ram_1_dout, register_file_1_r2d, register_file_1_stack_address, subtractor_1_out;

  assign bit_extender_1_out = {{13{1'b0}}, control_unit_1_inst_size};  // Bit_Extender bit_extender_1
  Adder #(.width(16)) adder_1 (.a(bit_extender_1_out), .b(register_1_q), .out(adder_1_out));  // open: cin, cout
  Register #(.width(16)) register_1 (.D(multiplexer_1_out), .en(1'b1), .clk(clock), .Q(register_1_q), .clr(reset));
  Multiplexer #(.width(16)) multiplexer_1 (
    .in0(adder_1_out), .in1({undriven_2, undriven}), .out(multiplexer_1_out), .sel(check_jump_1_jump));
  // ROM #(.addrWidth(16), .line("quad"), .misaligned("true")) rom_1: pin names not known; wires that end beside it: register_1_q
  Multiplexer #(.width(4)) multiplexer_2 (
    .in0({undriven_4[0], undriven_3[5:3]}), .in1({undriven_3[0], undriven_2[7:5]}), .out(multiplexer_2_out),
    .sel(control_unit_1_altregpos));
  assign bit_extender_2_out = {{16{1'b0}}, {undriven_2, undriven}};  // Bit_Extender bit_extender_2
  Multiplexer #(.width(4)) multiplexer_3 (
    .in0(undriven_4[4:1]), .in1(undriven_3[4:1]), .out(multiplexer_3_out), .sel(control_unit_1_altregpos));
  control_unit control_unit_1 (
    .opcode(undriven_5), .alucode({undriven_4, undriven_3[5]}), .memwrite(control_unit_1_memwrite),
    .jump(control_unit_1_jump), .memread(control_unit_1_memread), .regwritesrc(control_unit_1_regwritesrc),
    .altregpos(control_unit_1_altregpos), .regwritemod(control_unit_1_regwritemod),
    .regwrite(control_unit_1_regwrite), .memsrc(control_unit_1_memsrc), .alusrc(control_unit_1_alusrc),
    .inst_size(control_unit_1_inst_size), .usestack(control_unit_1_usestack),
    .incrstackaddr(control_unit_1_incrstackaddr));
  Multiplexer #(.width(32)) multiplexer_4 (
    .in0(multiplexer_9_out), .in1(multiplexer_15_out), .out(multiplexer_4_out),
    .sel(control_unit_1_regwritesrc));
  Multiplexer #(.width(32)) multiplexer_5 (
    .in0(register_file_1_r2d), .in1(bit_extender_2_out), .out({multiplexer_5_out_2, multiplexer_5_out}),
    .sel(control_unit_1_alusrc));
  Subtractor #(.width(32)) subtractor_1 (
    .a(register_file_1_stack_address), .b(32'h1), .out(subtractor_1_out));  // open: bin, bout
  Adder #(.width(32)) adder_2 (.a(register_file_1_stack_address), .b(32'h1), .out(adder_2_out));  // open: cin, cout
  register_file register_file_1 (
    .clock(clock), .WE(control_unit_1_regwrite), .reset(reset), .R1(multiplexer_3_out),
    .R2(multiplexer_2_out), .WD(multiplexer_4_out), .SWE(control_unit_1_usestack), .SWD(multiplexer_6_out),
    .R1D({register_file_1_r1d, register_file_1_r1d_2}), .R2D(register_file_1_r2d),
    .stack_address(register_file_1_stack_address));
  Multiplexer #(.width(32)) multiplexer_6 (
    .in0(subtractor_1_out), .in1(adder_2_out), .out(multiplexer_6_out), .sel(control_unit_1_incrstackaddr));
  Multiplexer #(.width(32)) multiplexer_7 (
    .in0({multiplexer_5_out_2, multiplexer_5_out}), .in1(register_file_1_stack_address),
    .out(multiplexer_7_out), .sel(control_unit_1_usestack));
  Multiplexer #(.width(32)) multiplexer_8 (
    .in0(multiplexer_7_out), .in1(multiplexer_6_out), .out(multiplexer_8_out),
    .sel(control_unit_1_incrstackaddr));
  Multiplexer #(.select(2), .width(32)) multiplexer_9 (
    .in0({32{1'b0}}), .in1({register_file_1_r1d, multiplexer_5_out}),
    .in2({register_file_1_r1d[23:8], multiplexer_5_out_2[7:0], multiplexer_5_out}),
    .in3({multiplexer_5_out_2, multiplexer_5_out}), .out(multiplexer_9_out), .sel(control_unit_1_regwritemod));
  check_jump check_jump_1 (
    .jump_cond(control_unit_1_jump), .eq_flag(flags_1_eq_out), .le_flag(flags_1_le_out),
    .jump(check_jump_1_jump));
  ALU alu_1 (
    .select_oper(undriven_4), .data_0({register_file_1_r1d, register_file_1_r1d_2}),
    .data_1({multiplexer_5_out_2, multiplexer_5_out}), .data(alu_1_data), .overflow(alu_1_overflow),
    .eq(alu_1_eq), .le(alu_1_le));
  Multiplexer #(.width(32)) multiplexer_10 (
    .in0(alu_1_data), .in1({register_file_1_r1d, register_file_1_r1d_2}), .out(multiplexer_10_out),
    .sel(control_unit_1_memsrc));
  or or_1 (or_1_out, control_unit_1_memwrite[3], control_unit_1_memwrite[2], control_unit_1_memwrite[1], control_unit_1_memwrite[0]);
  RAM #(.addrWidth(16), .asyncread("true"), .byteenables("byteEnables"), .clearpin("true"), .dataWidth(32), .\type ("nonvolatile")) ram_1 (
    .addr(multiplexer_8_out[15:0]), .we(or_1_out), .oe(1'b1), .clk(clock), .din(multiplexer_10_out),
    .dout(ram_1_dout), .clr(reset), .be3(or_2_out), .be2(or_3_out), .be1(or_4_out), .be0(or_5_out));
  flags flags_1 (
    .clock(clock), .reset(reset), .overflow(alu_1_overflow), .eq(alu_1_eq), .le(alu_1_le),
    .eq_out(flags_1_eq_out), .le_out(flags_1_le_out));  // open: overflow_out
  or or_2 (or_2_out, control_unit_1_memread[3], control_unit_1_memwrite[3]);
  or or_3 (or_3_out, control_unit_1_memread[2], control_unit_1_memwrite[2]);
  or or_4 (or_4_out, control_unit_1_memread[1], control_unit_1_memwrite[1]);
  or or_5 (or_5_out, control_unit_1_memread[0], control_unit_1_memwrite[0]);
  Multiplexer #(.width(8)) multiplexer_11 (
    .in0({8{1'b0}}), .in1(ram_1_dout[7:0]), .out(multiplexer_11_out), .sel(control_unit_1_memread[0]));
  Multiplexer #(.width(8)) multiplexer_12 (
    .in0({8{1'b0}}), .in1(ram_1_dout[15:8]), .out(multiplexer_12_out), .sel(control_unit_1_memread[1]));
  Multiplexer #(.width(8)) multiplexer_13 (
    .in0({8{1'b0}}), .in1(ram_1_dout[23:16]), .out(multiplexer_13_out), .sel(control_unit_1_memread[2]));
  Multiplexer #(.width(8)) multiplexer_14 (
    .in0({8{1'b0}}), .in1(ram_1_dout[31:24]), .out(multiplexer_14_out), .sel(control_unit_1_memread[3]));
  or or_6 (or_6_out, control_unit_1_memread[3], control_unit_1_memread[2], control_unit_1_memread[1], control_unit_1_memread[0]);
  assign or_7_out = {{24{1'b0}}, multiplexer_11_out} | {{16{1'b0}}, multiplexer_12_out, {8{1'b0}}} | {{8{1'b0}}, multiplexer_13_out, {16{1'b0}}} | {multiplexer_14_out, {24{1'b0}}};  // OR_Gate or_7, 32 bits wide
  Multiplexer #(.width(32)) multiplexer_15 (
    .in0(multiplexer_10_out), .in1(or_7_out), .out(multiplexer_15_out), .sel(or_6_out));

  // Notes on the sheet:
  //   contents of rom_1 (hex, n*v repeats v):
  //   0 20 88 88 0 3e 0 20 f0 0 0 24 0 11 f8 80
endmodule

module ALU (
  input  [4:0] select_oper,
  input  [31:0] data_0,
  input  [31:0] data_1,
  output [31:0] data,
  output overflow,
  output eq,
  output le
);

  wire adder_1_cout, adder_2_cout, comparator_1_eq, comparator_2_eq, comparator_3_lt, comparator_4_lt,
       comparator_5_eq, comparator_5_lt, comparator_6_eq, comparator_6_lt, comparator_7_eq, comparator_8_eq,
       comparator_9_eq, fpcomparator_1_p3, fpcomparator_1_p4, or_2_out, or_3_out, or_4_out,
       subtractor_1_bout, subtractor_2_bout, undriven, undriven_2, undriven_3, undriven_4;
  wire [31:0] adder_1_out, adder_2_out, and_1_out, divider_1_out, divider_1_rem, divider_2_out,
       divider_2_rem, fpadder_1_out, fpdivider_1_out, fpmultiplier_1_out, fpsubtractor_1_out,
       multiplier_1_cout, multiplier_1_out, multiplier_2_cout, multiplier_2_out, nand_1_out, nor_1_out,
       or_1_out, shifter_1_out, shifter_2_out, shifter_3_out, subtractor_1_out, subtractor_2_out, xor_1_out,
       xor_2_out;

  Comparator #(.mode("unsigned"), .width(32)) comparator_1 (
    .a({32{1'b0}}), .b(divider_2_rem), .eq(comparator_1_eq));  // open: gt, lt
  Comparator #(.mode("unsigned"), .width(32)) comparator_2 (
    .a({32{1'b0}}), .b(divider_1_rem), .eq(comparator_2_eq));  // open: gt, lt
  Comparator #(.mode("unsigned"), .width(32)) comparator_3 (
    .a({32{1'b0}}), .b(multiplier_2_cout), .lt(comparator_3_lt));  // open: gt, eq
  Comparator #(.mode("unsigned"), .width(32)) comparator_4 (
    .a({32{1'b0}}), .b(multiplier_1_cout), .lt(comparator_4_lt));  // open: gt, eq
  Adder #(.width(32)) adder_1 (.a(data_0), .b(data_1), .out(adder_1_out), .cout(adder_1_cout));  // open: cin
  Adder #(.width(32)) adder_2 (.a(data_0), .b(data_1), .out(adder_2_out), .cout(adder_2_cout));  // open: cin
  FPAdder fpadder_1 (.a(data_0), .b(data_1), .out(fpadder_1_out));
  Subtractor #(.width(32)) subtractor_1 (
    .a(data_0), .b(data_1), .out(subtractor_1_out), .bout(subtractor_1_bout));  // open: bin
  Subtractor #(.width(32)) subtractor_2 (
    .a(data_0), .b(data_1), .out(subtractor_2_out), .bout(subtractor_2_bout));  // open: bin
  FPSubtractor fpsubtractor_1 (.a(data_0), .b(data_1), .out(fpsubtractor_1_out));
  Multiplier #(.width(32)) multiplier_1 (
    .a(data_0), .b(data_1), .out(multiplier_1_out), .cout(multiplier_1_cout));  // open: cin
  Multiplier #(.width(32)) multiplier_2 (
    .a(data_0), .b(data_1), .out(multiplier_2_out), .cout(multiplier_2_cout));  // open: cin
  FPMultiplier fpmultiplier_1 (.a(data_0), .b(data_1), .out(fpmultiplier_1_out));
  Divider #(.width(32)) divider_1 (.a(data_0), .b(data_1), .out(divider_1_out), .rem(divider_1_rem));  // open: upper
  Divider #(.width(32)) divider_2 (.a(data_0), .b(data_1), .out(divider_2_out), .rem(divider_2_rem));  // open: upper
  FPDivider fpdivider_1 (.a(data_0), .b(data_1), .out(fpdivider_1_out));
  Shifter #(.width(32)) shifter_1 (.in(data_0), .\dist (data_1[4:0]), .out(shifter_1_out));
  Shifter #(.shift("lr"), .width(32)) shifter_2 (.in(data_0), .\dist (data_1[4:0]), .out(shifter_2_out));
  Shifter #(.shift("ar"), .width(32)) shifter_3 (.in(data_0), .\dist (data_1[4:0]), .out(shifter_3_out));
  assign or_1_out = data_0 | data_1;  // OR_Gate or_1, 32 bits wide
  assign nor_1_out = ~(data_0 | data_1);  // NOR_Gate nor_1, 32 bits wide
  assign xor_1_out = data_0 ^ data_1;  // XOR_Gate xor_1, 32 bits wide
  assign and_1_out = data_0 & data_1;  // AND_Gate and_1, 32 bits wide
  assign nand_1_out = ~(data_0 & data_1);  // NAND_Gate nand_1, 32 bits wide
  assign xor_2_out = data_0 ^ data_1;  // XOR_Gate xor_2, 32 bits wide
  // NOT_Gate not_1 is placed but not wired
  // NOT_Gate not_2 is placed but not wired
  Comparator #(.mode("unsigned"), .width(32)) comparator_5 (
    .a(data_0), .b(data_1), .eq(comparator_5_eq), .lt(comparator_5_lt));  // open: gt
  Comparator #(.width(32)) comparator_6 (
    .a(data_0), .b(data_1), .eq(comparator_6_eq), .lt(comparator_6_lt));  // open: gt
  // FPComparator fpcomparator_1: pin names not known; wires that end beside it: data_0, data_1, fpcomparator_1_p3, fpcomparator_1_p4
  or or_2 (or_2_out, comparator_5_eq, comparator_6_eq, fpcomparator_1_p3);
  or or_3 (or_3_out, comparator_5_lt, comparator_6_lt, fpcomparator_1_p4);
  Multiplexer #(.select(5), .width(32)) multiplexer_1 (
    .in0(adder_1_out), .in1(adder_2_out), .in2(fpadder_1_out), .in3(subtractor_1_out),
    .in4(subtractor_2_out), .in5(fpsubtractor_1_out), .in6(multiplier_1_out), .in7(multiplier_2_out),
    .in8(fpmultiplier_1_out), .in9(divider_1_out), .in10(divider_2_out), .in11(fpdivider_1_out),
    .in12(shifter_1_out), .in13(shifter_2_out), .in14(shifter_3_out), .in15(or_1_out), .in16(nor_1_out),
    .in17(xor_1_out), .in18(and_1_out), .in19(nand_1_out), .in20(xor_2_out), .out(data), .sel(select_oper));  // open: in21, in22, in23, in24, in25, in26, in27, in28, in29, in30, in31
  Comparator #(.width(5)) comparator_7 (.a(select_oper), .b(5'b10110), .eq(comparator_7_eq));  // open: gt, lt
  Comparator #(.width(5)) comparator_8 (.a(select_oper), .b(5'b10111), .eq(comparator_8_eq));  // open: gt, lt
  Comparator #(.width(5)) comparator_9 (.a(select_oper), .b(5'b11000), .eq(comparator_9_eq));  // open: gt, lt
  or or_4 (or_4_out, comparator_7_eq, comparator_8_eq, comparator_9_eq);
  and and_2 (eq, or_4_out, or_2_out);
  and and_3 (le, or_4_out, or_3_out);
  Multiplexer #(.select(5)) multiplexer_2 (
    .in0(adder_1_cout), .in1(adder_2_cout), .in2(undriven_4), .in3(subtractor_1_bout),
    .in4(subtractor_2_bout), .in5(undriven_3), .in6(comparator_4_lt), .in7(comparator_3_lt),
    .in8(undriven_2), .in9(comparator_2_eq), .in10(comparator_1_eq), .in11(undriven), .in12(1'b0),
    .in13(1'b0), .in14(1'b0), .out(overflow), .sel(select_oper));  // open: in15, in16, in17, in18, in19, in20, in21, in22, in23, in24, in25, in26, in27, in28, in29, in30, in31
endmodule

module register_file (
  input  clock,
  input  WE,
  input  reset,
  input  [3:0] R1,
  input  [3:0] R2,
  input  [31:0] WD,
  input  SWE,
  input  [31:0] SWD,
  output [31:0] R1D,
  output [31:0] R2D,
  output [31:0] stack_address
);

  wire DMX0, DMX1, DMX2, DMX3, DMX4, DMX5, DMX6, DMX7, DMX8, DMX9, DMX10, DMX11, DMX12, DMX13, DMX14, DMX15,
       DMX16, DMX17, DMX18, DMX19, DMX20, DMX21, DMX22, DMX23, DMX24, DMX25, DMX26, DMX27, DMX28, DMX29,
       DMX30, DMX31, or_1_out;
  wire [31:0] multiplexer_1_out, register_1_q, register_2_q, register_3_q, register_4_q, register_5_q,
       register_6_q, register_7_q, register_8_q, register_9_q, register_10_q, register_11_q, register_12_q,
       register_13_q, register_14_q, register_15_q, register_17_q, register_18_q, register_19_q,
       register_20_q, register_21_q, register_22_q, register_23_q, register_24_q, register_25_q,
       register_26_q, register_27_q, register_28_q, register_29_q, register_30_q, register_31_q,
       register_32_q;

  Register #(.width(32)) register_1 (.D(WD), .en(DMX0), .clk(clock), .Q(register_1_q), .clr(reset));
  Register #(.width(32)) register_2 (.D(WD), .en(DMX1), .clk(clock), .Q(register_2_q), .clr(reset));
  Register #(.width(32)) register_3 (.D(WD), .en(DMX2), .clk(clock), .Q(register_3_q), .clr(reset));
  Register #(.width(32)) register_4 (.D(WD), .en(DMX3), .clk(clock), .Q(register_4_q), .clr(reset));
  Register #(.width(32)) register_5 (.D(WD), .en(DMX4), .clk(clock), .Q(register_5_q), .clr(reset));
  Register #(.width(32)) register_6 (.D(WD), .en(DMX5), .clk(clock), .Q(register_6_q), .clr(reset));
  Register #(.width(32)) register_7 (.D(WD), .en(DMX6), .clk(clock), .Q(register_7_q), .clr(reset));
  Register #(.width(32)) register_8 (.D(WD), .en(DMX7), .clk(clock), .Q(register_8_q), .clr(reset));
  Demultiplexer #(.select(5)) demultiplexer_1 (
    .out0(DMX0), .out1(DMX1), .out2(DMX2), .out3(DMX3), .out4(DMX4), .out5(DMX5), .out6(DMX6), .out7(DMX7),
    .out8(DMX8), .out9(DMX9), .out10(DMX10), .out11(DMX11), .out12(DMX12), .out13(DMX13), .out14(DMX14),
    .out15(DMX15), .out16(DMX16), .out17(DMX17), .out18(DMX18), .out19(DMX19), .out20(DMX20), .out21(DMX21),
    .out22(DMX22), .out23(DMX23), .out24(DMX24), .out25(DMX25), .out26(DMX26), .out27(DMX27), .out28(DMX28),
    .out29(DMX29), .out30(DMX30), .out31(DMX31), .in(WE), .sel({1'b0, R1}));
  Multiplexer #(.width(32)) multiplexer_1 (.in0(WD), .in1(SWD), .out(multiplexer_1_out), .sel(SWE));
  Register #(.width(32)) register_9 (.D(WD), .en(DMX8), .clk(clock), .Q(register_9_q), .clr(reset));
  Register #(.width(32)) register_10 (.D(WD), .en(DMX9), .clk(clock), .Q(register_10_q), .clr(reset));
  Register #(.width(32)) register_11 (.D(WD), .en(DMX10), .clk(clock), .Q(register_11_q), .clr(reset));
  Register #(.width(32)) register_12 (.D(WD), .en(DMX11), .clk(clock), .Q(register_12_q), .clr(reset));
  Register #(.width(32)) register_13 (.D(WD), .en(DMX12), .clk(clock), .Q(register_13_q), .clr(reset));
  Register #(.width(32)) register_14 (.D(WD), .en(DMX13), .clk(clock), .Q(register_14_q), .clr(reset));
  Register #(.width(32)) register_15 (.D(WD), .en(DMX14), .clk(clock), .Q(register_15_q), .clr(reset));
  Register #(.width(32)) register_16 (
    .D(multiplexer_1_out), .en(or_1_out), .clk(clock), .Q(stack_address), .clr(reset));
  or or_1 (or_1_out, SWE, DMX15);
  Register #(.width(32)) register_17 (.D(WD), .en(DMX16), .clk(clock), .Q(register_17_q), .clr(reset));
  Register #(.width(32)) register_18 (.D(WD), .en(DMX17), .clk(clock), .Q(register_18_q), .clr(reset));
  Register #(.width(32)) register_19 (.D(WD), .en(DMX18), .clk(clock), .Q(register_19_q), .clr(reset));
  Register #(.width(32)) register_20 (.D(WD), .en(DMX19), .clk(clock), .Q(register_20_q), .clr(reset));
  Register #(.width(32)) register_21 (.D(WD), .en(DMX20), .clk(clock), .Q(register_21_q), .clr(reset));
  Register #(.width(32)) register_22 (.D(WD), .en(DMX21), .clk(clock), .Q(register_22_q), .clr(reset));
  Register #(.width(32)) register_23 (.D(WD), .en(DMX22), .clk(clock), .Q(register_23_q), .clr(reset));
  Register #(.width(32)) register_24 (.D(WD), .en(DMX23), .clk(clock), .Q(register_24_q), .clr(reset));
  Register #(.width(32)) register_25 (.D(WD), .en(DMX24), .clk(clock), .Q(register_25_q), .clr(reset));
  Register #(.width(32)) register_26 (.D(WD), .en(DMX25), .clk(clock), .Q(register_26_q), .clr(reset));
  Register #(.width(32)) register_27 (.D(WD), .en(DMX26), .clk(clock), .Q(register_27_q), .clr(reset));
  Register #(.width(32)) register_28 (.D(WD), .en(DMX27), .clk(clock), .Q(register_28_q), .clr(reset));
  Register #(.width(32)) register_29 (.D(WD), .en(DMX28), .clk(clock), .Q(register_29_q), .clr(reset));
  Register #(.width(32)) register_30 (.D(WD), .en(DMX29), .clk(clock), .Q(register_30_q), .clr(reset));
  Register #(.width(32)) register_31 (.D(WD), .en(DMX30), .clk(clock), .Q(register_31_q), .clr(reset));
  Register #(.width(32)) register_32 (.D(WD), .en(DMX31), .clk(clock), .Q(register_32_q), .clr(reset));
  Multiplexer #(.select(5), .width(32)) multiplexer_2 (
    .in0(register_1_q), .in1(register_2_q), .in2(register_3_q), .in3(register_4_q), .in4(register_5_q),
    .in5(register_6_q), .in6(register_7_q), .in7(register_8_q), .in8(register_9_q), .in9(register_10_q),
    .in10(register_11_q), .in11(register_12_q), .in12(register_13_q), .in13(register_14_q),
    .in14(register_15_q), .in15(stack_address), .in16(register_17_q), .in17(register_18_q),
    .in18(register_19_q), .in19(register_20_q), .in20(register_21_q), .in21(register_22_q),
    .in22(register_23_q), .in23(register_24_q), .in24(register_25_q), .in25(register_26_q),
    .in26(register_27_q), .in27(register_28_q), .in28(register_29_q), .in29(register_30_q),
    .in30(register_31_q), .in31(register_32_q), .out(R1D), .sel({1'b0, R1}));
  Multiplexer #(.select(5), .width(32)) multiplexer_3 (
    .in0(register_1_q), .in1(register_2_q), .in2(register_3_q), .in3(register_4_q), .in4(register_5_q),
    .in5(register_6_q), .in6(register_7_q), .in7(register_8_q), .in8(register_9_q), .in9(register_10_q),
    .in10(register_11_q), .in11(register_12_q), .in12(register_13_q), .in13(register_14_q),
    .in14(register_15_q), .in15(stack_address), .in16(register_17_q), .in17(register_18_q),
    .in18(register_19_q), .in19(register_20_q), .in20(register_21_q), .in21(register_22_q),
    .in22(register_23_q), .in23(register_24_q), .in24(register_25_q), .in25(register_26_q),
    .in26(register_27_q), .in27(register_28_q), .in28(register_29_q), .in29(register_30_q),
    .in30(register_31_q), .in31(register_32_q), .out(R2D), .sel({1'b0, R2}));

  // Other names for the same wires on the sheet: RS[3:0] = R1
endmodule

module multiplexor6bit (
  input  [5:0] selector,
  input  [31:0] in_2,
  input  [31:0] in_3,
  input  [31:0] in_4,
  input  [31:0] in_5,
  input  [31:0] in_6,
  input  [31:0] in_7,
  input  [31:0] in_8,
  input  [31:0] in_9,
  input  [31:0] in_10,
  input  [31:0] in_11,
  input  [31:0] in_12,
  input  [31:0] in_13,
  input  [31:0] in_14,
  input  [31:0] in_15,
  input  [31:0] in_16,
  input  [31:0] in_17,
  input  [31:0] in_18,
  input  [31:0] in_19,
  input  [31:0] in_20,
  input  [31:0] in_21,
  input  [31:0] in_22,
  input  [31:0] in_23,
  input  [31:0] in_24,
  input  [31:0] in_25,
  input  [31:0] in_26,
  input  [31:0] in_27,
  input  [31:0] in_28,
  input  [31:0] in_29,
  input  [31:0] in_30,
  input  [31:0] in_31,
  input  [31:0] in_32,
  input  [31:0] in_33,
  input  [31:0] in_34,
  input  [31:0] in_35,
  input  [31:0] in_36,
  input  [31:0] in_37,
  input  [31:0] in_38,
  input  [31:0] in_39,
  input  [31:0] in_40,
  input  [31:0] in_41,
  input  [31:0] in_42,
  input  [31:0] in_43,
  input  [31:0] in_44,
  input  [31:0] in_45,
  input  [31:0] in_46,
  input  [31:0] in_47,
  input  [31:0] in_48,
  input  [31:0] in_49,
  input  [31:0] in_50,
  input  [31:0] in_51,
  input  [31:0] in_52,
  input  [31:0] in_53,
  input  [31:0] in_54,
  input  [31:0] in_55,
  input  [31:0] in_56,
  input  [31:0] in_57,
  input  [31:0] in_58,
  input  [31:0] in_59,
  input  [31:0] in_60,
  input  [31:0] in_61,
  input  [31:0] in_62,
  input  [31:0] in_63,
  input  [31:0] in_64,
  input  [31:0] in_65,
  output [31:0] out_66
);

  wire not_1_out;
  wire [31:0] multiplexer_1_out, multiplexer_2_out;

  Multiplexer #(.select(5), .width(32)) multiplexer_1 (
    .in0(in_2), .in1(in_3), .in2(in_4), .in3(in_5), .in4(in_6), .in5(in_7), .in6(in_8), .in7(in_9),
    .in8(in_10), .in9(in_11), .in10(in_12), .in11(in_13), .in12(in_14), .in13(in_15), .in14(in_16),
    .in15(in_17), .in16(in_18), .in17(in_19), .in18(in_20), .in19(in_21), .in20(in_22), .in21(in_23),
    .in22(in_24), .in23(in_25), .in24(in_26), .in25(in_27), .in26(in_28), .in27(in_29), .in28(in_30),
    .in29(in_31), .in30(in_32), .in31(in_33), .out(multiplexer_1_out), .sel(selector[4:0]));
  Multiplexer #(.select(5), .width(32)) multiplexer_2 (
    .in0(in_34), .in1(in_35), .in2(in_36), .in3(in_37), .in4(in_38), .in5(in_39), .in6(in_40), .in7(in_41),
    .in8(in_42), .in9(in_43), .in10(in_44), .in11(in_45), .in12(in_46), .in13(in_47), .in14(in_48),
    .in15(in_49), .in16(in_50), .in17(in_51), .in18(in_52), .in19(in_53), .in20(in_54), .in21(in_55),
    .in22(in_56), .in23(in_57), .in24(in_58), .in25(in_59), .in26(in_60), .in27(in_61), .in28(in_62),
    .in29(in_63), .in30(in_64), .in31(in_65), .out(multiplexer_2_out), .sel(selector[4:0]));
  not not_1 (not_1_out, selector[5]);
  gate32bit gate32bit_1 (.enable(selector[5]), .data(multiplexer_2_out), .out_3(out_66));
  gate32bit gate32bit_2 (.enable(not_1_out), .data(multiplexer_1_out), .out_3(out_66));
endmodule

module gate32bit (
  input  enable,
  input  [31:0] data,
  output [31:0] out_3
);

  wire [31:0] and_1_out, bit_extender_1_out;

  assign bit_extender_1_out = {{31{enable}}, enable};  // Bit_Extender bit_extender_1
  assign and_1_out = bit_extender_1_out & data;  // AND_Gate and_1, 32 bits wide
  assign out_3 = enable ? and_1_out : 32'bz;  // Controlled_Buffer controlled_buffer_1
endmodule

module control_unit (
  input  [4:0] opcode,
  input  [5:0] alucode,
  output [3:0] memwrite,
  output [4:0] jump,
  output [3:0] memread,
  output regwritesrc,
  output altregpos,
  output [1:0] regwritemod,
  output regwrite,
  output memsrc,
  output alusrc,
  output [2:0] inst_size,
  output usestack,
  output incrstackaddr
);

  wire comparator_1_eq, comparator_2_eq, comparator_3_eq, comparator_4_eq, comparator_5_eq, comparator_6_eq,
       comparator_7_eq, comparator_8_eq, comparator_9_eq, comparator_10_eq, comparator_11_eq,
       comparator_12_eq, comparator_13_eq, comparator_14_eq, comparator_15_eq, comparator_16_eq,
       comparator_17_eq, comparator_18_eq, comparator_19_eq, comparator_20_eq, nor_1_out, nor_2_out,
       nor_3_out, not_1_out, or_1_out, or_2_out, or_3_out, or_4_out, or_5_out, or_6_out, or_9_out, or_10_out,
       type_ident_1_adr, type_ident_1_arl, type_ident_1_asr, type_ident_1_dr, type_ident_1_rl,
       type_ident_1_sl, type_ident_1_sr;

  Comparator #(.mode("unsigned"), .width(5)) comparator_1 (
    .a(opcode), .b(5'b00011), .eq(comparator_1_eq));  // open: gt, lt
  Comparator #(.mode("unsigned"), .width(5)) comparator_2 (
    .a(opcode), .b(5'b00010), .eq(comparator_2_eq));  // open: gt, lt
  Comparator #(.mode("unsigned"), .width(5)) comparator_3 (
    .a(opcode), .b(5'b00001), .eq(comparator_3_eq));  // open: gt, lt
  Comparator #(.mode("unsigned"), .width(5)) comparator_4 (
    .a(opcode), .b(5'b00110), .eq(comparator_4_eq));  // open: gt, lt
  Comparator #(.mode("unsigned"), .width(5)) comparator_5 (
    .a(opcode), .b(5'b00101), .eq(comparator_5_eq));  // open: gt, lt
  Comparator #(.mode("unsigned"), .width(5)) comparator_6 (
    .a(opcode), .b(5'b00100), .eq(comparator_6_eq));  // open: gt, lt
  Comparator #(.mode("unsigned"), .width(5)) comparator_7 (
    .a(opcode), .b(5'b01011), .eq(comparator_7_eq));  // open: gt, lt
  Comparator #(.mode("unsigned"), .width(5)) comparator_8 (
    .a(opcode), .b(5'b01001), .eq(comparator_8_eq));  // open: gt, lt
  Comparator #(.mode("unsigned"), .width(5)) comparator_9 (
    .a(opcode), .b(5'b00111), .eq(comparator_9_eq));  // open: gt, lt
  Comparator #(.mode("unsigned"), .width(5)) comparator_10 (
    .a(opcode), .b(5'b01100), .eq(comparator_10_eq));  // open: gt, lt
  Comparator #(.mode("unsigned"), .width(5)) comparator_11 (
    .a(opcode), .b(5'b01010), .eq(comparator_11_eq));  // open: gt, lt
  Comparator #(.mode("unsigned"), .width(5)) comparator_12 (
    .a(opcode), .b(5'b01000), .eq(comparator_12_eq));  // open: gt, lt
  nor nor_1 (nor_1_out, comparator_1_eq, comparator_2_eq, or_1_out);
  or or_1 (or_1_out, comparator_3_eq, comparator_20_eq);
  nor nor_2 (nor_2_out, comparator_4_eq, comparator_5_eq, or_2_out);
  or or_2 (or_2_out, comparator_6_eq, incrstackaddr);
  assign memwrite = nor_1_out ? 4'b0000 : 4'bz;  // Controlled_Buffer controlled_buffer_1
  assign memwrite = comparator_1_eq ? 4'b0001 : 4'bz;  // Controlled_Buffer controlled_buffer_2
  assign memwrite = comparator_2_eq ? 4'b0011 : 4'bz;  // Controlled_Buffer controlled_buffer_3
  assign memwrite = or_1_out ? 4'b1111 : 4'bz;  // Controlled_Buffer controlled_buffer_4
  not not_1 (not_1_out, nor_2_out);
  assign memread = nor_2_out ? 4'b0000 : 4'bz;  // Controlled_Buffer controlled_buffer_5
  assign memread = comparator_4_eq ? 4'b0001 : 4'bz;  // Controlled_Buffer controlled_buffer_6
  assign memread = comparator_5_eq ? 4'b0011 : 4'bz;  // Controlled_Buffer controlled_buffer_7
  assign memread = or_2_out ? 4'b1111 : 4'bz;  // Controlled_Buffer controlled_buffer_8
  or or_3 (or_3_out, comparator_7_eq, comparator_10_eq);
  or or_4 (or_4_out, comparator_8_eq, comparator_11_eq);
  or or_5 (or_5_out, comparator_9_eq, comparator_12_eq);
  nor nor_3 (nor_3_out, or_3_out, or_4_out, or_5_out);
  assign regwritemod = nor_3_out ? 2'b00 : 2'bz;  // Controlled_Buffer controlled_buffer_9
  assign regwritemod = or_3_out ? 2'b01 : 2'bz;  // Controlled_Buffer controlled_buffer_10
  assign regwritemod = or_4_out ? 2'b10 : 2'bz;  // Controlled_Buffer controlled_buffer_11
  assign regwritemod = or_5_out ? 2'b11 : 2'bz;  // Controlled_Buffer controlled_buffer_12
  or or_6 (or_6_out, comparator_10_eq, comparator_11_eq, comparator_12_eq);
  type_ident type_ident_1 (
    .opcode(opcode), .alucode(alucode), .SL(type_ident_1_sl), .SR(type_ident_1_sr), .DR(type_ident_1_dr),
    .RL(type_ident_1_rl), .ASR(type_ident_1_asr), .ADR(type_ident_1_adr), .ARL(type_ident_1_arl));
  or or_7 (altregpos, type_ident_1_asr, type_ident_1_adr, type_ident_1_arl);
  Comparator #(.mode("unsigned"), .width(4)) comparator_13 (
    .a(opcode[4:1]), .b(4'b1000), .eq(comparator_13_eq));  // open: gt, lt
  Comparator #(.mode("unsigned"), .width(4)) comparator_14 (
    .a(opcode[4:1]), .b(4'b1001), .eq(comparator_14_eq));  // open: gt, lt
  Comparator #(.mode("unsigned"), .width(4)) comparator_15 (
    .a(opcode[4:1]), .b(4'b1010), .eq(comparator_15_eq));  // open: gt, lt
  Comparator #(.mode("unsigned"), .width(4)) comparator_16 (
    .a(opcode[4:1]), .b(4'b1011), .eq(comparator_16_eq));  // open: gt, lt
  Comparator #(.mode("unsigned"), .width(4)) comparator_17 (
    .a(opcode[4:1]), .b(4'b1100), .eq(comparator_17_eq));  // open: gt, lt
  Comparator #(.mode("unsigned"), .width(4)) comparator_18 (
    .a(opcode[4:1]), .b(4'b1101), .eq(comparator_18_eq));  // open: gt, lt
  Comparator #(.mode("unsigned"), .width(4)) comparator_19 (
    .a(opcode[4:1]), .b(4'b1110), .eq(comparator_19_eq));  // open: gt, lt
  Comparator #(.mode("unsigned"), .width(4)) comparator_20 (
    .a(opcode[4:1]), .b(4'b0111), .eq(comparator_20_eq));  // open: gt, lt
  Comparator #(.mode("unsigned"), .width(4)) comparator_21 (
    .a(opcode[4:1]), .b(4'b1111), .eq(incrstackaddr));  // open: gt, lt
  or or_8 (usestack, comparator_20_eq, incrstackaddr);
  or or_9 (or_9_out, type_ident_1_sr, type_ident_1_dr, type_ident_1_asr);
  or or_10 (or_10_out, type_ident_1_sl, type_ident_1_rl, type_ident_1_arl);
  or or_11 (jump[1], comparator_14_eq, comparator_15_eq, comparator_16_eq, comparator_17_eq, comparator_18_eq, comparator_19_eq);
  or or_12 (jump[0], comparator_13_eq, jump[1]);
  or or_13 (jump[2], comparator_16_eq, comparator_17_eq, comparator_18_eq, comparator_19_eq);
  or or_14 (jump[3], comparator_14_eq, comparator_17_eq, comparator_19_eq);
  or or_15 (jump[4], comparator_18_eq, comparator_19_eq);
  or or_16 (memsrc, type_ident_1_sr, type_ident_1_dr, type_ident_1_rl);
  or or_17 (regwritesrc, or_6_out, altregpos, not_1_out);
  or or_18 (regwrite, altregpos, not_1_out, type_ident_1_rl);
  or or_19 (alusrc, opcode[0], or_6_out, type_ident_1_arl);
  assign inst_size = or_9_out ? 3'b010 : 3'bz;  // Controlled_Buffer controlled_buffer_13
  assign inst_size = type_ident_1_adr ? 3'b011 : 3'bz;  // Controlled_Buffer controlled_buffer_14
  assign inst_size = or_10_out ? 3'b100 : 3'bz;  // Controlled_Buffer controlled_buffer_15
endmodule

module type_ident (
  input  [4:0] opcode,
  input  [5:0] alucode,
  output SL,
  output SR,
  output DR,
  output RL,
  output ASR,
  output ADR,
  output ARL
);

  wire and_1_out, and_2_out, and_3_out, and_4_out, and_5_out, and_7_out, comparator_1_eq, comparator_2_eq,
       comparator_3_eq, comparator_4_gt, comparator_5_lt, comparator_6_eq, comparator_7_eq, comparator_8_eq,
       comparator_9_eq, comparator_10_eq, not_1_out, not_2_out;

  not not_1 (not_1_out, opcode[0]);
  and and_1 (and_1_out, opcode[1], opcode[2], opcode[3]);
  and and_2 (and_2_out, not_1_out, opcode[4]);
  and and_3 (and_3_out, opcode[0], opcode[4]);
  and and_4 (and_4_out, opcode[0], and_1_out);
  and and_5 (and_5_out, and_1_out, not_2_out);
  not not_2 (not_2_out, opcode[0]);
  Comparator #(.mode("unsigned"), .width(5)) comparator_1 (
    .a(opcode), .b({5{1'b0}}), .eq(comparator_1_eq));  // open: gt, lt
  Comparator #(.mode("unsigned"), .width(5)) comparator_2 (
    .a(alucode[5:1]), .b(5'b10100), .eq(comparator_2_eq));  // open: gt, lt
  Comparator #(.mode("unsigned"), .width(5)) comparator_3 (
    .a(alucode[5:1]), .b(5'b10101), .eq(comparator_3_eq));  // open: gt, lt
  Comparator #(.mode("unsigned"), .width(5)) comparator_4 (
    .a(opcode), .b({5{1'b0}}), .gt(comparator_4_gt));  // open: eq, lt
  Comparator #(.mode("unsigned"), .width(5)) comparator_5 (
    .a(opcode), .b(5'b01000), .lt(comparator_5_lt));  // open: gt, eq
  Comparator #(.mode("unsigned"), .width(5)) comparator_6 (
    .a(opcode), .b(5'b01001), .eq(comparator_6_eq));  // open: gt, lt
  Comparator #(.mode("unsigned"), .width(5)) comparator_7 (
    .a(opcode), .b(5'b01011), .eq(comparator_7_eq));  // open: gt, lt
  and and_6 (ARL, comparator_1_eq, alucode[0]);
  or or_1 (ASR, comparator_2_eq, comparator_3_eq);
  or or_2 (SL, and_4_out, and_3_out);
  and and_7 (and_7_out, comparator_4_gt, comparator_5_lt);
  or or_3 (DR, and_7_out, comparator_6_eq, comparator_7_eq);
  or or_4 (SR, and_5_out, and_2_out);
  Comparator #(.mode("unsigned"), .width(5)) comparator_8 (
    .a(opcode), .b(5'b01000), .eq(comparator_8_eq));  // open: gt, lt
  Comparator #(.mode("unsigned"), .width(5)) comparator_9 (
    .a(opcode), .b(5'b01010), .eq(comparator_9_eq));  // open: gt, lt
  Comparator #(.mode("unsigned"), .width(5)) comparator_10 (
    .a(opcode), .b(5'b01100), .eq(comparator_10_eq));  // open: gt, lt
  or or_5 (RL, comparator_8_eq, comparator_9_eq, comparator_10_eq);
  nor nor_1 (ADR, SR, SL, DR, RL, ARL, ASR);
endmodule

module flags (
  input  clock,
  input  reset,
  input  overflow,
  input  eq,
  input  le,
  output overflow_out,
  output eq_out,
  output le_out
);

  Register #(.width(1)) register_1 (.D(overflow), .en(1'b1), .clk(clock), .Q(overflow_out), .clr(reset));
  Register #(.width(1)) register_2 (.D(eq), .en(1'b1), .clk(clock), .Q(eq_out), .clr(reset));
  Register #(.width(1)) register_3 (.D(le), .en(1'b1), .clk(clock), .Q(le_out), .clr(reset));
endmodule

module check_jump (
  input  [4:0] jump_cond,
  input  eq_flag,
  input  le_flag,
  output jump
);

  wire and_1_out, not_1_out, not_2_out, or_1_out, or_2_out, or_3_out, xnor_1_out, xnor_2_out;

  not not_1 (not_1_out, jump_cond[1]);
  not not_2 (not_2_out, jump_cond[2]);
  or or_1 (or_1_out, not_1_out, xnor_1_out);
  xnor xnor_1 (xnor_1_out, jump_cond[3], eq_flag);
  or or_2 (or_2_out, not_2_out, xnor_2_out);
  xnor xnor_2 (xnor_2_out, jump_cond[4], le_flag);
  and and_1 (and_1_out, or_1_out, or_2_out);
  buf or_3 (or_3_out, and_1_out);  // OR_Gate
  and and_2 (jump, jump_cond[0], or_3_out);
endmodule
